# Fritzing sketch control_light_using_button_Fritzing (saved by Fritzing 0.8.3b)
breadboards: 1

parts:
  元件1 = Arduino Uno (Rev3)
  S1 = Pushbutton [package="[THT]"]
  R1 = Resistor [tolerance=±5% resistance=220 package=THT]
  LED1 = LED - 5mm [color="Red (633nm)" package="5 mm [THT]"]
  R2 = Resistor [tolerance=±5% resistance=220 package=THT]

nets:
  N1: 元件1.GND, S1.Pin_3, S1.Pin_4, LED1.cathode
  N2: 元件1.D9_PWM, R1.Pin_1
  N3: 元件1.D2, R2.Pin_1
  N4: S1.Pin_1, S1.Pin_2, R2.Pin_0
  N5: R1.Pin_0, LED1.anode
