# Fritzing sketch control_light_using_sound_Fritzing (saved by Fritzing 0.8.3b)
breadboards: 1

parts:
  元件1 = Arduino Uno (Rev3)
  R1 = Resistor [tolerance=±5% resistance=220 package=THT]
  LED1 = LED - 5mm [color="Red (633nm)" package="5 mm [THT]"]

nets:
  N1: 元件1.GND, R1.Pin_0
  N2: 元件1.D11_PWM/MOSI, LED1.anode
  N3: R1.Pin_1, LED1.cathode
